# Fritzing sketch 05.full_scheme_02_two_motors (saved by Fritzing 0.9.4)
breadboards: 2

parts:
  Teensy1 = Teensy 4.0
  IC1 = H-Bridge [package=THT]
  VCC1 = Battery block 9V
  M1 = DC Motor
  Part1 = Adafruit DRV2605L [part_number="Adafruit #2305"]
  M3 = DC Motor
  R3 = Slide Potentiometer [maximum_resistance=10kΩ]
  RE1 = Rotary Encoder [package=THT]
  Part2 = Adafruit DRV2605L [part_number="Adafruit #2305"]
  RE2 = Rotary Encoder [package=THT]
  C1 = Ceramic Capacitor [capacitance=0.1µF voltage=16V package="1206 [SMD, multilayer]"]
  C3 = Ceramic Capacitor [capacitance="100 nF" package="1206 [SMD, multilayer]"]
  C4 = Ceramic Capacitor [capacitance=100nF package="200 mil [THT, multilayer]"]
  C5 = Ceramic Capacitor [capacitance=100nF package="200 mil [THT, multilayer]"]
  C6 = Ceramic Capacitor [capacitance=100nF package="200 mil [THT, multilayer]"]
  C8 = Ceramic Capacitor [capacitance="100 nF" package="1206 [SMD, multilayer]"]  # not connected
  U1 = Chip antenna [package=antenna-chip2]
  U2 = Chip antenna [package=antenna-chip2]
  U3 = Chip antenna [package=antenna-chip2]
  U4 = Chip antenna [package=antenna-chip2]
  R2 = Slide Potentiometer [maximum_resistance=10kΩ]

nets:
  GND: Teensy1.pin_1, Teensy1.pin_17, Teensy1.pin_32, IC1.GND1, IC1.GND2, IC1.GND3, IC1.GND4, VCC1.-, Part1.GND, Part1.IN/TRIG, R3.leg1, RE1.EncoderPinC, RE1.SwitchPinE, Part2.GND, Part2.IN/TRIG, RE2.EncoderPinC, RE2.SwitchPinE, C1.1, C3.1, C4.1, C5.1, C6.1, R2.leg1
  N1: Teensy1.pin_2, U3.SIGNAL
  N2: Teensy1.pin_3, RE1.EncoderPinA
  N3: Teensy1.pin_4, RE1.EncoderPinB
  N4: Teensy1.pin_5, RE1.SwitchrPinD
  N5: Teensy1.pin_6, RE2.EncoderPinA
  N6: Teensy1.pin_7, RE2.EncoderPinB
  N7: Teensy1.pin_8, RE2.SwitchrPinD
  N8: Teensy1.pin_9, U2.SIGNAL
  N9: Teensy1.pin_10, IC1.1A
  N10: Teensy1.pin_11, IC1.2A
  N11: Teensy1.pin_12, U1.SIGNAL
  N12: Teensy1.pin_13, IC1.4A
  N13: Teensy1.pin_14, IC1.3A
  N14: Teensy1.pin_16, Teensy1.pin_31, R3.leg2, C3.0, R2.leg2
  N15: Teensy1.pin_21, IC1.1_2EN
  N16: Teensy1.pin_22, IC1.3_4EN
  N17: Teensy1.pin_23, Part2.SCL
  N18: Teensy1.pin_24, Part2.SDA
  N19: Teensy1.pin_25, Part1.SDA
  N20: Teensy1.pin_26, Part1.SCL
  N21: Teensy1.pin_27, R2.wiper
  N22: Teensy1.pin_28, R3.wiper
  N23: Teensy1.pin_30, U4.SIGNAL
  N24: Teensy1.pin33, IC1.VCC1, Part2.VIN, C4.0, C5.0, C6.0
  N25: IC1.1Y, M1.pin_1
  N26: IC1.2Y, M1.pin_2
  N27: IC1.VCC2, VCC1.+, C1.0
  N28: IC1.3Y, M3.pin_2
  N29: IC1.4Y, M3.pin_1

notes:
  fader 1

custom parts:
  Teensy 4.0: The Teensy is a complete USB-based microcontoller development system, in a very small footprint, capable of implementing many types of projects. All programming is done via the USB port. No special programmer is needed, only a standard micro-USB cable and a PC or Macintosh with a USB port.
  Adafruit DRV2605L: The DRV2605 from TI is a fancy little motor driver. Rather than controlling a stepper motor or DC motor, its designed specifically for controlling haptic motors - buzzers and vibration motors. Normally one would just turn those kinds of motors on and off, but this driver has the ability to have various effects when driving a vibe motor. For example, ramping the vibration level up and down,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
  Rotary Encoder: Rotary Encoder from ALPSec11e with switch.
